// Logisim project lab4solution.circ as structural Verilog: 1 circuit, main circuit main
module main (
  input  z,
  input  y,
  input  x,
  output cout,
  output sum
);

  wire not_1_out;

  Multiplexer #(.select(2), .enable("false")) multiplexer_1 (
    .in0(1'b0), .in1(z), .in2(z), .in3(1'b1), .out(cout), .sel({x, y}));
  not not_1 (not_1_out, z);
  Multiplexer #(.select(2), .enable("false")) multiplexer_2 (
    .in0(z), .in1(not_1_out), .in2(not_1_out), .in3(z), .out(sum), .sel({x, y}));
endmodule
