// Logisim project lab6solution.circ as structural Verilog: 5 circuits, main circuit main
module main (
  input  in_1,
  input  [2:0] in_2
);

  wire clock_1_out, clock_2_out;
  wire [1:0] Odd_Even_output, register_1_q;
  wire [2:0] Coin_output, register_2_q;

  Odd_Even_Circuit Odd_Even (.state(register_1_q), .\input (in_1), .\output (Odd_Even_output));
  Register #(.width(2)) register_1 (.D(Odd_Even_output), .Q(register_1_q), .clk(clock_1_out));  // open: en, clr
  Clock clock_1 (.out(clock_1_out));
  Coin_Circuit Coin (.\input (register_2_q[1:0]), .state(in_2), .\output (Coin_output));
  Clock clock_2 (.out(clock_2_out));
  Register #(.width(3)) register_2 (.D(Coin_output), .Q(register_2_q), .clk(clock_2_out));  // open: en, clr
  // Pins of 2 and 3 bits meet at register_2_q
endmodule

module Odd_Even_Circuit (
  input  [1:0] state,
  input  \input ,
  output [1:0] \output 
);

  not not_1 (\output [0], state[0]);
  xor xor_1 (\output [1], state[1], \input );
endmodule

module Coin_Circuit (
  input  [1:0] \input ,
  input  [2:0] state,
  output [2:0] \output 
);

  wire and_1_out, not_1_out, or_1_out, or_2_out, xnor_1_out;

  and and_1 (and_1_out, \input [0], \input [1]);
  not not_1 (not_1_out, \input [0]);
  or or_1 (or_1_out, \input [0], \input [1]);
  xnor xnor_1 (xnor_1_out, \input [1], \input [0]);
  or or_2 (or_2_out, not_1_out, \input [1]);
  Multiplexer #(.select(3)) multiplexer_1 (
    .in0(or_2_out), .in1(\input [0]), .in2(xnor_1_out), .in3(\input [0]), .in4(xnor_1_out), .in5(and_1_out),
    .in6(and_1_out), .in7(1'b1), .out(\output [0]), .sel(state));  // open: en
  Multiplexer #(.select(3)) multiplexer_2 (
    .in0(\input [0]), .in1(1'b1), .in2(or_2_out), .in3(\input [1]), .in4(or_1_out), .in5(1'b1), .in6(1'b1),
    .in7(1'b1), .out(\output [1]), .sel(state));  // open: en
  Multiplexer #(.select(3)) multiplexer_3 (
    .in0(\input [1]), .in1(\input [1]), .in2(or_1_out), .in3(1'b1), .in4(1'b1), .in5(1'b1), .in6(1'b1),
    .in7(1'b1), .out(\output [2]), .sel(state));  // open: en
endmodule

module Odd_Even_w__MUX (
  input  \input ,
  input  [1:0] state,
  output [1:0] out_3
);

  wire not_1_out;

  not not_1 (not_1_out, \input );
  Multiplexer #(.select(2)) multiplexer_1 (
    .in0(\input ), .in1(\input ), .in2(not_1_out), .in3(not_1_out), .out(out_3[1]), .sel(state));  // open: en
  Multiplexer #(.select(2)) multiplexer_2 (
    .in0(1'b1), .in1(1'b0), .in2(1'b1), .in3(1'b0), .out(out_3[0]), .sel(state));  // open: en
endmodule

module Sort_of_easier_Coin_Circuit (
  input  [1:0] \input ,
  input  [2:0] state,
  output [2:0] out_3
);

  Multiplexer #(.select(5)) multiplexer_1 (
    .in0(1'b0), .in1(1'b0), .in2(1'b1), .in3(1'b1), .in4(1'b0), .in5(1'b0), .in6(1'b1), .in7(1'b1),
    .in8(1'b0), .in9(1'b1), .in10(1'b1), .in11(1'b1), .in12(1'b1), .in13(1'b1), .in14(1'b1), .in15(1'b1),
    .in16(1'b1), .in17(1'b1), .in18(1'b1), .in19(1'b1), .in20(1'b1), .in21(1'b1), .in22(1'b1), .in23(1'b1),
    .in24(1'b1), .in25(1'b1), .in26(1'b1), .in27(1'b1), .in28(1'b1), .in29(1'b1), .in30(1'b1), .in31(1'b1),
    .out(out_3[2]), .sel({state, \input }));  // open: en
  Multiplexer #(.select(5)) multiplexer_2 (
    .in0(1'b0), .in1(1'b1), .in2(1'b0), .in3(1'b1), .in4(1'b1), .in5(1'b1), .in6(1'b1), .in7(1'b1),
    .in8(1'b1), .in9(1'b0), .in10(1'b1), .in11(1'b1), .in12(1'b0), .in13(1'b0), .in14(1'b1), .in15(1'b1),
    .in16(1'b0), .in17(1'b1), .in18(1'b1), .in19(1'b1), .in20(1'b1), .in21(1'b1), .in22(1'b1), .in23(1'b1),
    .in24(1'b1), .in25(1'b1), .in26(1'b1), .in27(1'b1), .in28(1'b1), .in29(1'b1), .in30(1'b1), .in31(1'b1),
    .out(out_3[1]), .sel({state, \input }));  // open: en
  Multiplexer #(.select(5)) multiplexer_3 (
    .in0(1'b1), .in1(1'b0), .in2(1'b1), .in3(1'b1), .in4(1'b0), .in5(1'b1), .in6(1'b0), .in7(1'b1),
    .in8(1'b1), .in9(1'b0), .in10(1'b0), .in11(1'b1), .in12(1'b0), .in13(1'b1), .in14(1'b0), .in15(1'b1),
    .in16(1'b1), .in17(1'b0), .in18(1'b0), .in19(1'b1), .in20(1'b0), .in21(1'b0), .in22(1'b0), .in23(1'b1),
    .in24(1'b0), .in25(1'b0), .in26(1'b0), .in27(1'b1), .in28(1'b1), .in29(1'b1), .in30(1'b1), .in31(1'b1),
    .out(out_3[0]), .sel({state, \input }));  // open: en
endmodule
