// Logisim project lecture9.circ as structural Verilog: 1 circuit, main circuit main
module main (
  input  a,
  input  in_2,
  input  b,
  input  [7:0] in_4,
  input  S_prime,
  input  R_prime,
  output a_2,
  output q,
  output a_prime,
  output q_2,
  output b_prime_b__prime,
  output a_prime_b__prime,
  output [7:0] out_13,
  output q_3,
  output q_prime
);

  wire and_1_out, clock_1_out;

  buf buffer_1 (a_2, a);
  not not_1 (a_prime, a);
  and and_1 (and_1_out, b, a);
  nand nand_1 (b_prime_b__prime, b, b);
  not not_2 (a_prime_b__prime, and_1_out);
  nand nand_2 (q_3, S_prime, q_prime);
  nand nand_3 (q_prime, q_3, R_prime);
  Clock clock_1 (.out(clock_1_out));
  D_Flip_Flop d_ff_1 (.clk(clock_1_out), .D(in_2), .Q(q));  // open: Qn, preset, en, reset
  D_Flip_Flop d_ff_2 (.clk(clock_1_out), .D(in_2), .Q(q_2));  // open: Qn, preset, en, reset
  Register register_1 (.D(in_4), .Q(out_13), .clk(clock_1_out));  // open: en, clr

  // Notes on the sheet:
  //   S'R' Latch
endmodule
